// Digital circuit bw8.dig as structural Verilog
module bw8 (
  input  SaveFlags,
  input  UseBankRegister,
  input  nCodeAccess,
  input  nKernelMode,
  input  [1:0] in_9,
  output Carry,
  output Zero,
  output Overflow,
  output Negative
);

  wire AccessType, add_carry, AluDecoder_d, and_3_out, AssertSystemBus, carry_t, clk, InterruptDecoder_d,
       JumpDecoder_d, left_shift_carry, left_sign, LoadA, LoadB, LoadBR, LoadC, LoadD, LoadIR, LoadOffset,
       LoadPC_H, LoadPC_L, LoadSP_H, LoadSP_L, LoadTPtr_H, LoadTPtr_L, LoadTReg, LoadX_H, LoadX_L, LoadY_H,
       LoadY_L, multiplexer_11_out, negative_t, or_1_out, or_2_out, PointerWriteBackSelect, PrimaryDecoder_d,
       RegisterLoadEnable, RegisterWriteBackSelect, ResetSequencer, ResultSelect, right_shift_carry,
       ToggleExtension;
  wire [1:0] AdderSelect, CarrySelect, OffsetMode, PointerLoadEnable, ShiftSelect;
  wire [2:0] AluFunction, driver_3_out, JumpCondition, LeftSelect, mcr, PointerLoadSelect, PointerSelect,
       RegisterLoadSelect, RightSelect, seq;
  wire [2:1] new_status;
  wire [3:0] br, driver_2_out, LogicSelect, mbr, multiplexer_1_out_2, multiplexer_15_out;
  wire [6:0] result, shift, SHL_out;
  wire [7:0] areg, ASR_out, breg, creg, DataBus, decoder_1_out_0, decoder_2_out_0, decoder_3_out_0, dreg, ir,
       \logic , mdi, mdo, MemoryData, multiplexer_1_out, multiplexer_2_out, multiplexer_4_out,
       multiplexer_5_out, multiplexer_6_out, multiplexer_12_out, multiplexer_13_out, off, temp;
  wire [7:1] SHR_out;
  wire [7:4] Flags, undriven, undriven_2;
  wire [11:11] Extended_Opcode_q;
  wire [13:3] undriven_3;
  wire [15:0] add_2_s, Address, bitextender_1_out, mar, multiplexer_7_out, multiplexer_8_out, pc, sp, tp, xp,
       yp;
  wire [15:8] multiplexer_16_out;

  Counter #(.Bits(3)) Sequencer (.en(1'b1), .C(clk), .clr(ResetSequencer), .out(seq));  // open: ovf
  Register #(.Bits(8)) Instruction_Register (.D(DataBus), .C(clk), .en(LoadIR), .Q(ir));
  T_FF Extended_Opcode (.T(ToggleExtension), .C(clk), .Q(Extended_Opcode_q[11]));  // open: nQ
  Decoder #(.Selector_Bits(3)) decoder_1 (
    .sel(PointerLoadSelect), .out_0(decoder_1_out_0[7]), .out_1(decoder_1_out_0[6]),
    .out_2(decoder_1_out_0[5]), .out_3(decoder_1_out_0[4]), .out_4(decoder_1_out_0[3]),
    .out_5(decoder_1_out_0[2]), .out_6(decoder_1_out_0[1]), .out_7(decoder_1_out_0[0]));
  Decoder #(.Selector_Bits(3)) decoder_2 (
    .sel(PointerLoadSelect), .out_0(decoder_2_out_0[0]), .out_1(decoder_2_out_0[1]),
    .out_2(decoder_2_out_0[2]), .out_3(decoder_2_out_0[3]), .out_4(decoder_2_out_0[4]),
    .out_5(decoder_2_out_0[5]), .out_6(decoder_2_out_0[6]), .out_7(decoder_2_out_0[7]));
  ROM #(.AddrBits(12)) PrimaryDecoder (.A({Extended_Opcode_q[11], ir, seq}), .sel(1'b1), .D(PrimaryDecoder_d));
  D_FF #(.Bits(2)) Mode (.D(in_9), .C(clk), .Q(undriven_3[4:3]));  // open: nQ
  Multiplexer #(.Bits(8)) multiplexer_1 (
    .sel(PointerLoadEnable[1]), .in_0({8{1'b0}}), .in_1(decoder_1_out_0),
    .out({multiplexer_1_out[7:5], multiplexer_1_out_2, multiplexer_1_out[0]}));
  Multiplexer #(.Bits(8)) multiplexer_2 (
    .sel(PointerLoadEnable[0]), .in_0({8{1'b0}}), .in_1(decoder_2_out_0), .out(multiplexer_2_out));
  ROM #(.AddrBits(14)) InterruptDecoder (.A({undriven_3, seq}), .sel(1'b1), .D(InterruptDecoder_d));
  or or_1 (or_1_out, undriven_3[3], undriven_3[4]);
  ROM #(.AddrBits(7)) JumpDecoder (.A({Negative, Overflow, Zero, Carry, JumpCondition}), .sel(1'b1), .D(JumpDecoder_d));
  Decoder #(.Selector_Bits(3)) decoder_3 (
    .sel(RegisterLoadSelect), .out_0(decoder_3_out_0[0]), .out_1(decoder_3_out_0[1]),
    .out_2(decoder_3_out_0[2]), .out_3(decoder_3_out_0[3]), .out_4(decoder_3_out_0[4]),
    .out_5(decoder_3_out_0[5]), .out_6(decoder_3_out_0[6]), .out_7(decoder_3_out_0[7]));
  Multiplexer multiplexer_3 (
    .sel(or_1_out), .in_0(PrimaryDecoder_d), .in_1(InterruptDecoder_d), .out(RegisterLoadSelect[0]));
  and and_1 (undriven[4], multiplexer_1_out[0], JumpDecoder_d);
  and and_2 (undriven_2[4], multiplexer_2_out[0], JumpDecoder_d);
  Multiplexer #(.Bits(8)) multiplexer_4 (
    .sel(RegisterLoadEnable), .in_0({8{1'b0}}), .in_1(decoder_3_out_0), .out(multiplexer_4_out));
  ROM #(.AddrBits(3)) AluDecoder (.A(AluFunction), .sel(1'b1), .D(AluDecoder_d));
  D_FF d_ff_1 (.D(multiplexer_1_out_2[0]), .C(clk), .Q(LoadTPtr_H));  // open: nQ
  D_FF d_ff_2 (.D(multiplexer_2_out[1]), .C(clk), .Q(LoadTPtr_L));  // open: nQ
  D_FF d_ff_3 (.D(multiplexer_4_out[0]), .C(clk), .Q(LoadA));  // open: nQ
  D_FF d_ff_4 (.D(AluDecoder_d), .C(clk), .Q(ShiftSelect[0]));  // open: nQ
  // Probe Instruction Register on ir
  // Probe Sequencer on seq
  // Probe on areg
  // Probe on breg
  // Probe on creg
  // Probe on dreg
  // Probe on temp
  // Probe on pc
  // Probe on sp
  // Probe on xp
  // Probe on yp
  // Probe on tp
  Register #(.Bits(8)) GPR_A (.D(multiplexer_16_out), .C(clk), .en(LoadA), .Q(areg));
  Register #(.Bits(8)) GPR_B (.D(multiplexer_16_out), .C(clk), .en(LoadB), .Q(breg));
  Register #(.Bits(8)) GPR_C (.D(multiplexer_16_out), .C(clk), .en(LoadC), .Q(creg));
  Register #(.Bits(8)) GPR_D (.D(multiplexer_16_out), .C(clk), .en(LoadD), .Q(dreg));
  Register #(.Bits(8)) u_Temp (.D(multiplexer_16_out), .C(clk), .en(LoadTReg), .Q(temp));
  Register #(.Bits(8), .isProgramCounter("true")) register_1 (
    .D(multiplexer_7_out[15:8]), .C(clk), .en(LoadPC_H), .Q(pc[15:8]));
  Register #(.Bits(8), .isProgramCounter("true")) register_2 (
    .D(multiplexer_7_out[15:8]), .C(clk), .en(LoadSP_H), .Q(sp[15:8]));
  Register #(.Bits(8), .isProgramCounter("true")) register_3 (
    .D(multiplexer_7_out[15:8]), .C(clk), .en(LoadX_H), .Q(xp[15:8]));
  Register #(.Bits(8), .isProgramCounter("true")) register_4 (
    .D(multiplexer_7_out[15:8]), .C(clk), .en(LoadY_H), .Q(yp[15:8]));
  Register #(.Bits(8), .isProgramCounter("true")) register_5 (
    .D(multiplexer_7_out[15:8]), .C(clk), .en(LoadTPtr_H), .Q(tp[15:8]));
  Register #(.Bits(8), .isProgramCounter("true")) register_6 (
    .D(multiplexer_7_out[7:0]), .C(clk), .en(LoadPC_L), .Q(pc[7:0]));
  Register #(.Bits(8), .isProgramCounter("true")) register_7 (
    .D(multiplexer_7_out[7:0]), .C(clk), .en(LoadSP_L), .Q(sp[7:0]));
  Register #(.Bits(8), .isProgramCounter("true")) register_8 (
    .D(multiplexer_7_out[7:0]), .C(clk), .en(LoadX_L), .Q(xp[7:0]));
  Register #(.Bits(8), .isProgramCounter("true")) register_9 (
    .D(multiplexer_7_out[7:0]), .C(clk), .en(LoadY_L), .Q(yp[7:0]));
  Register #(.Bits(8), .isProgramCounter("true")) register_10 (
    .D(multiplexer_7_out[7:0]), .C(clk), .en(LoadTPtr_L), .Q(tp[7:0]));
  Multiplexer #(.Selector_Bits(3), .Bits(8)) multiplexer_5 (
    .sel(LeftSelect), .in_0(areg), .in_1(breg), .in_2(creg), .in_3(dreg), .in_4(temp), .in_5({8{1'b0}}),
    .in_6({8{1'b0}}), .in_7({8{1'b0}}), .out(multiplexer_5_out));
  Multiplexer #(.Selector_Bits(3), .Bits(8)) multiplexer_6 (
    .sel(RightSelect), .in_0(areg), .in_1(breg), .in_2(creg), .in_3(dreg), .in_4(temp), .in_5({8{1'b0}}),
    .in_6({8{1'b0}}), .in_7({8{1'b0}}), .out(multiplexer_6_out));
  Multiplexer #(.Bits(16)) multiplexer_7 (
    .sel(PointerWriteBackSelect), .in_0({multiplexer_16_out, multiplexer_16_out}), .in_1(add_2_s),
    .out(multiplexer_7_out));
  Multiplexer #(.Selector_Bits(3), .Bits(16)) multiplexer_8 (
    .sel(PointerSelect), .in_0(pc), .in_1(sp), .in_2(xp), .in_3(yp), .in_4(tp), .in_5(16'h3), .in_6(16'h6),
    .in_7(16'h9), .out(multiplexer_8_out));
  BarrelShifter #(.Bits(8)) SHL (.in(multiplexer_5_out), .shift(4'b0001), .out({left_shift_carry, SHL_out}));
  BarrelShifter #(.Bits(8), .direction("right")) SHR (
    .in(multiplexer_5_out), .shift(4'b0001), .out({SHR_out, right_shift_carry}));
  BarrelShifter #(.Bits(8), .barrelShifterMode("arithmetic"), .direction("right")) ASR (
    .in(multiplexer_5_out), .shift(4'b0001), .out(ASR_out));
  Multiplexer #(.Selector_Bits(2), .Bits(8)) multiplexer_9 (
    .sel(ShiftSelect), .in_0({left_shift_carry, SHL_out}), .in_1({SHR_out, right_shift_carry}),
    .in_2(ASR_out), .in_3(multiplexer_5_out), .out({left_sign, shift}));
  ROM #(.AddrBits(20), .Bits(8)) Logic_Unit (
    .A({LogicSelect, multiplexer_6_out, multiplexer_5_out}), .sel(1'b1), .D(\logic ));
  Multiplexer #(.Selector_Bits(2)) multiplexer_10 (
    .sel(CarrySelect), .in_0(1'b0), .in_1(add_carry), .in_2(right_shift_carry), .in_3(left_shift_carry),
    .out(carry_t));
  Register #(.Bits(8)) Offset_Register (.D(multiplexer_16_out), .C(clk), .en(LoadOffset), .Q(off));
  Add #(.Bits(8)) add_1 (
    .a({left_sign, shift}), .b(\logic ), .c_i(multiplexer_11_out), .s({negative_t, result}), .c_o(add_carry));
  Register #(.Bits(8)) Status (
    .D({4'b0000, negative_t, new_status, carry_t}), .C(clk), .en(SaveFlags),
    .Q({Flags, Negative, Overflow, Zero, Carry}));
  Comparator #(.Bits(8)) comparator_1 (.a({negative_t, result}), .b({8{1'b0}}), .eq(new_status[1]));  // open: gt, lt
  Multiplexer #(.Selector_Bits(2)) multiplexer_11 (
    .sel(AdderSelect), .in_0(1'b0), .in_1(1'b1), .in_2(Carry), .in_3(1'b0), .out(multiplexer_11_out));
  Multiplexer #(.Selector_Bits(2), .Bits(8)) multiplexer_12 (
    .sel(OffsetMode), .in_0({8{1'b0}}), .in_1(off), .in_2(8'h1), .in_3({8{1'b1}}), .out(multiplexer_12_out));
  Register #(.Bits(4)) Bank_Register (.D(multiplexer_16_out[11:8]), .C(clk), .en(LoadBR), .Q(br));
  and and_3 (and_3_out, UseBankRegister, nCodeAccess);
  // Probe on {negative_t, result}
  // Probe on {left_sign, shift}
  // Probe on \logic 
  BitExtender bitextender_1 (.in(multiplexer_12_out), .out(bitextender_1_out));
  or or_2 (or_2_out, and_3_out, nKernelMode);
  Multiplexer #(.Bits(8)) multiplexer_13 (
    .sel(ResultSelect), .in_1({negative_t, result}), .out(multiplexer_13_out));  // open: in_0
  Multiplexer #(.Selector_Bits(3)) multiplexer_14 (
    .sel({negative_t, left_sign, \logic [7]}), .in_0(1'b0), .in_1(1'b0), .in_2(1'b0), .in_3(1'b1),
    .in_4(1'b1), .in_5(1'b0), .in_6(1'b0), .in_7(1'b0), .out(new_status[2]));
  // Probe on br
  // Probe on off
  Add #(.Bits(16)) add_2 (.a(bitextender_1_out), .b(multiplexer_8_out), .c_i(1'b0), .s(add_2_s));  // open: c_o
  Multiplexer #(.Bits(4)) multiplexer_15 (.sel(or_2_out), .in_0(4'b0000), .in_1(br), .out(multiplexer_15_out));
  Multiplexer #(.Bits(8)) multiplexer_16 (
    .sel(RegisterWriteBackSelect), .in_0(multiplexer_13_out), .in_1(mdi), .out(multiplexer_16_out));
  D_FF #(.Bits(8)) Data_Register__Out (.D(multiplexer_13_out), .C(clk), .Q(mdo));  // open: nQ
  // Probe on mar
  // Probe on mbr
  // Probe on mcr
  D_FF #(.Bits(16)) Addr_Register (.D(add_2_s), .C(clk), .Q(mar));  // open: nQ
  D_FF #(.Bits(4)) Bank_Register_2 (.D(multiplexer_15_out), .C(clk), .Q(mbr));  // open: nQ
  D_FF #(.Bits(3)) Control_Register (.D({nCodeAccess, AccessType, nKernelMode}), .C(clk), .Q(mcr));  // open: nQ
  D_FF #(.Bits(8)) Data_Register__In (.D(MemoryData), .C(clk), .Q(mdi));  // open: nQ
  assign Address = AssertSystemBus ? mar : 16'bz;  // Driver driver_1
  Driver #(.Bits(4)) driver_2 (.in(mbr), .out(driver_2_out));  // open: en
  Driver #(.Bits(3)) driver_3 (.in(mcr), .out(driver_3_out));  // open: en
  // Probe on mdi
  // Probe on mdo
  assign MemoryData = 1'b0 ? mdo : 8'bz;  // Driver driver_4
  ROM #(.AddrBits(16), .Bits(8)) rom_1 (.A(Address), .sel(1'b1), .D(MemoryData));
  Button button_1 (.out(clk));
  // Pins of 1 and 8 bits meet at multiplexer_4_out
  // Pins of 1 and 8 bits meet at {LoadIR, LoadTReg, LoadBR, LoadOffset, LoadD, LoadC, LoadB, LoadA}
  // Pins of 4 and 8 bits meet at {Flags, Negative, Overflow, Zero, Carry}
  // Pins of 8 and 14 bits meet at {undriven_3, seq}
  // Pins of 1 and 8 bits meet at {undriven, multiplexer_1_out_2}
  // Pins of 1 and 5 bits meet at {LoadPC_H, LoadSP_H, LoadX_H, LoadY_H, LoadTPtr_H}
  // Pins of 1 and 8 bits meet at {undriven_2, multiplexer_2_out[4:1]}
  // Pins of 1 and 5 bits meet at {LoadPC_L, LoadSP_L, LoadX_L, LoadY_L, LoadTPtr_L}

  // Other names for the same wires on the sheet: new_status (some bits) = {negative_t, carry_t}; cf = Carry;
  //   Flags[3:0] = {Negative, Overflow, Zero, Carry}; InterruptMode[1:0] = in_9; right_sign = \logic [7];
  //   nIOAccess = AccessType; overflow_t = new_status[2]; result[7] = negative_t; shift[7] = left_sign;
  //   zero_t = new_status[1]

  // Notes on the sheet:
  //   Control
  //   TODO: Implement system
  //   control flag latches
  //   TODO: Add support for UBR flag
  //   A Register
  //   B Register
  //   C Register
  //   D Register
  //   Temp Register
  //   Program Counter
  //   Stack Pointer
  //   X Pointer
  //   Y Pointer
  //   Temp Pointer
  //   Pointer File
  //   Interrupt Vectors
  //   Register File
  //   Arithmetic & Logic Unit
  //   Address Generation Unit
  //   Status
  //   contents of Logic_Unit (hex, n*v repeats v):
  //   5
  //   Result
  //   Shift
  //   Logic
  //   8-bit WriteBack
  //   Reset
  //   Bank Register
  //   Offset Register
  //   16-bit WriteBack
  //   Addr Register
  //   Control Register
  //   Data Register (In)
  //   Data Register (Out)
  //   Memory & IO
  //   contents of rom_1 (hex, n*v repeats v):
  //   5
endmodule
